# Fritzing sketch schematic (saved by Fritzing 0.9.3b)

parts:
  Part1 = Arduino Mega 2560 (Rev3)
  ZS-042_RTC1 = ZS-042 RTC Module
  U1 = L298 [package=multiwatt15]
  U2 = L298 [package=multiwatt15]  # not connected
  M1 = Stepper Motor - Bipolar
  M2 = Stepper Motor - Bipolar  # not connected

nets:
  N1: Part1.D18/TX1, ZS-042_RTC1.SQW
  GND: Part1.GND, ZS-042_RTC1.GND, U1.GND
  N2: Part1.D2_PWM, U1.IN1
  N3: Part1.D3_PWM, U1.IN2
  N4: Part1.D4_PWM, U1.IN3
  N5: Part1.D5_PWM, U1.IN4
  5V: Part1.5V, ZS-042_RTC1.VCC
  N6: Part1.D24, ZS-042_RTC1.SCL
  N7: Part1.D25, ZS-042_RTC1.SDA
  N8: U1.OUT1, M1.A
  N9: U1.OUT2, M1.C
  N10: U1.OUT3, M1.B
  N11: U1.OUT4, M1.D
